# Fritzing sketch fritzing diagram (saved by Fritzing 0.9.9b)
breadboards: 1

parts:
  OLED_I2C1 = OLED 128x64 I2C Monochrome Display
  Argon1 = Particle Argon
  Part1 = 12 NeoPixel Ring [part_number=1643]
  Neopixel1 = Adafruit RBG Smart Neopixel [package="DIP (Dual Inline) [THT]"]
  Neopixel2 = Adafruit RBG Smart Neopixel [package="DIP (Dual Inline) [THT]"]
  Neopixel3 = Adafruit RBG Smart Neopixel [package="DIP (Dual Inline) [THT]"]
  Neopixel4 = Adafruit RBG Smart Neopixel [package="DIP (Dual Inline) [THT]"]
  IC1 = MSGEQ7 [package=soic8]

nets:
  N1: OLED_I2C1.SDA, Argon1.SDA
  N2: OLED_I2C1.SCK, Argon1.SCL
  VDD: OLED_I2C1.VDD, Argon1.3.3V
  GND: OLED_I2C1.GND, Argon1.GND, Part1.GND, Neopixel1.G, Neopixel2.G, Neopixel3.G, Neopixel4.G, IC1.GND
  N3: Argon1.A2, IC1.RESET
  N4: Argon1.A3, IC1.STROBE
  N5: Argon1.A4, IC1.DCOUT
  N6: Argon1.D8, Neopixel1.In
  VDD_2: Argon1.VUSB, Part1.VDD, Neopixel1.+, Neopixel2.+, Neopixel3.+, Neopixel4.+, IC1.VDD
  N7: Part1.IN, Neopixel1.O
  N8: Part1.OUT, Neopixel2.In
  N9: Neopixel2.O, Neopixel4.In
  N10: Neopixel3.In, Neopixel4.O

custom parts:
  Particle Argon: The Argon is a powerful Wi-Fi enabled development board that can act as either a standalone Wi-Fi endpoint or Wi-Fi enabled gateway for Particle Mesh networks. It is based on the Nordic nRF52840 and has built-in battery charging circuitry so it’s easy to connect a Li-Po and deploy your local network in minutes. The Argon is great for connecting existing projects to the Particle Device Cloud or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
  12 NeoPixel Ring: 12 ultra bright smart LED NeoPixels are arranged in a circle with 1.5" (37mm) outer diameter. The rings are 'chainable' - connect the output pin of one to the input pin of another. Use only one microcontroller pin to control as many as you can chain together! Each LED is addressable as the driver chip is inside the LED. Each one has ~18mA constant current drive so the color will be very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
